# Fritzing sketch TripleAndPortCmos4073 (saved by Fritzing 0.9.0b)
circuit board: 16cm x 10cm
breadboards: 1

parts:
  RLED1_1 = Resistor [tolerance=±5% resistance=1k package=THT]
  CMOS_1 = mystery part, 14 pins [chip_label="CMOS4073 (3AND)"]
  Arduino1 = Arduino Uno (Rev3)
  LED1_1 = LED - 5mm [color="Red (633nm)" package="5 mm [THT]"]
  LED1_2 = LED - 5mm [color="Red (633nm)" package="5 mm [THT]"]
  LED1_3 = LED - 5mm [color="Red (633nm)" package="5 mm [THT]"]
  LED1OUT = LED - 5mm [color="Red (633nm)" package="5 mm [THT]"]
  RLED1_2 = Resistor [tolerance=±5% resistance=1k package=THT]
  RLED1_3 = Resistor [tolerance=±5% resistance=1k package=THT]
  RLEDOUT = Resistor [tolerance=±5% resistance=1k package=THT]
  R1_1PD = Resistor [tolerance=±5% resistance=10k package=THT]
  R1_2PD = Resistor [tolerance=±5% resistance=10k package=THT]
  R1_3PD = Resistor [tolerance=±5% resistance=10k package=THT]
  part = Resistor [tolerance=±5% resistance=220 package=THT]  # not connected

nets:
  N1: RLED1_1.Pin_0, LED1_1.cathode
  N2: RLED1_1.Pin_1, CMOS_1.pin7, Arduino1.GND, RLED1_2.Pin_1, RLED1_3.Pin_1, RLEDOUT.Pin_1, R1_1PD.Pin_1, R1_2PD.Pin_1, R1_3PD.Pin_1
  N3: CMOS_1.pin3, Arduino1.D4, LED1_1.anode, R1_1PD.Pin_0
  N4: CMOS_1.pin4, LED1_2.anode, R1_2PD.Pin_0
  N5: CMOS_1.pin5, Arduino1.D2, LED1_3.anode, R1_3PD.Pin_0
  N6: CMOS_1.pin6, LED1OUT.anode
  N7: LED1_2.cathode, RLED1_2.Pin_0
  N8: LED1_3.cathode, RLED1_3.Pin_0
  N9: LED1OUT.cathode, RLEDOUT.Pin_0
